// Logisim project lcpu.circ as structural Verilog
module main (
);

  wire ALU_cout, ALU_eq, ALU_gt, ALU_lt, ALU_zero, clock_1_out, control_1_cin, control_1_dset,
       control_1_fetch, control_1_fset, control_1_iset, control_1_pcload, control_1_sinv, control_1_ssel,
       control_1_tinv, control_1_tsel, control_1_write, not_1_out, or_1_out;
  wire [1:0] control_1_dsel, control_1_pcop;
  wire [2:0] ID_dreg, ID_sreg, ID_treg;
  wire [3:0] control_1_aop;
  wire [6:0] ID_op;
  wire [15:0] ALU_dval, imm_q, multiplexer_1_out, multiplexer_2_out, multiplexer_3_out, PC_pc, ram_1_data,
       RF_sval, RF_tval;

  pc_16bit PC (
    .pcop(control_1_pcop), .pcset(control_1_pcload), .clock(clock_1_out), .pc(PC_pc));  // open: addr, reset, pc_1
  // Probe on PC_pc
  RAM #(.addrWidth(16), .dataWidth(16)) ram_1 (
    .addr(PC_pc), .data(ram_1_data), .clk(clock_1_out), .ld(not_1_out));  // open: sel, clr
  not not_1 (not_1_out, control_1_write);
  Clock clock_1 (.out(clock_1_out));
  // Probe on ram_1_data
  id_16bit ID (
    .inst(ram_1_data), .fetch(control_1_fetch), .clock(clock_1_out), .op(ID_op), .dreg(ID_dreg),
    .sreg(ID_sreg), .treg(ID_treg));
  // Probe on ID_op
  control control_1 (
    .cop(ID_op), .clock(clock_1_out), .ssel(control_1_ssel), .tsel(control_1_tsel), .cin(control_1_cin),
    .sinv(control_1_sinv), .tinv(control_1_tinv), .aop(control_1_aop), .dset(control_1_dset),
    .fset(control_1_fset), .iset(control_1_iset), .fetch(control_1_fetch), .pcload(control_1_pcload),
    .pcop(control_1_pcop), .write(control_1_write), .dsel(control_1_dsel));  // open: timm
  Register #(.width(16)) imm (.D(ram_1_data), .en(control_1_iset), .Q(imm_q), .clk(clock_1_out));  // open: clr
  Multiplexer #(.select(2), .width(16)) multiplexer_1 (
    .in0(imm_q), .in1(ram_1_data), .in2(ALU_dval), .out(multiplexer_1_out), .sel(control_1_dsel));  // open: in3, en
  registerFile_8x16bit RF (
    .dreg(ID_dreg), .sreg(ID_sreg), .treg(ID_treg), .dval(multiplexer_1_out), .dset(control_1_dset),
    .clock(clock_1_out), .sval(RF_sval), .tval(RF_tval));  // open: reg0, reg1, reg2, reg3, reg4, reg5, reg6, reg7
  // Probe on ID_treg
  Multiplexer #(.width(16)) multiplexer_2 (
    .in0(RF_sval), .in1(imm_q), .out(multiplexer_2_out), .sel(control_1_ssel));  // open: en
  Multiplexer #(.width(16)) multiplexer_3 (
    .in0(RF_tval), .in1({16{1'b0}}), .out(multiplexer_3_out), .sel(or_1_out));  // open: en
  or or_1 (or_1_out, control_1_tsel, ID_treg[0]);
  // Probe on or_1_out
  // Probe on multiplexer_2_out
  // Probe on multiplexer_3_out
  alu_16bit ALU (
    .sval(multiplexer_2_out), .tval(multiplexer_3_out), .cin(control_1_cin), .sinv(control_1_sinv),
    .tinv(control_1_tinv), .aop(control_1_aop), .gt(ALU_gt), .eq(ALU_eq), .lt(ALU_lt), .cout(ALU_cout),
    .zero(ALU_zero), .dval(ALU_dval));
  // Probe on ALU_dval
  // Probe on control_1_aop
  fu fu_1 (
    .gt(ALU_gt), .eq(ALU_eq), .lt(ALU_lt), .cout(ALU_cout), .zero(ALU_zero), .fset(control_1_fset));  // open: br, clock, gt_2, eq_2, lt_2, cout_2, zero_2, br_2
endmodule

// Registers
module registerFile_8x16bit (
  input  [2:0] dreg,
  input  clock,
  input  [2:0] sreg,
  input  [2:0] treg,
  input  dset,
  input  [15:0] dval,
  output [15:0] reg0,
  output [15:0] reg1,
  output [15:0] reg2,
  output [15:0] reg3,
  output [15:0] reg4,
  output [15:0] reg5,
  output [15:0] reg6,
  output [15:0] reg7,
  output [15:0] sval,
  output [15:0] tval
);

  wire demultiplexer_1_out0, demultiplexer_1_out1, demultiplexer_1_out2, demultiplexer_1_out3,
       demultiplexer_1_out4, demultiplexer_1_out5, demultiplexer_1_out6, demultiplexer_1_out7;

  Demultiplexer #(.select(3)) demultiplexer_1 (
    .out0(demultiplexer_1_out0), .out1(demultiplexer_1_out1), .out2(demultiplexer_1_out2),
    .out3(demultiplexer_1_out3), .out4(demultiplexer_1_out4), .out5(demultiplexer_1_out5),
    .out6(demultiplexer_1_out6), .out7(demultiplexer_1_out7), .in(dset), .sel(dreg));  // open: en
  Register #(.width(16)) register_1 (.D(dval), .en(demultiplexer_1_out0), .Q(reg0), .clk(clock));  // open: clr
  Register #(.width(16)) register_2 (.D(dval), .en(demultiplexer_1_out1), .Q(reg1), .clk(clock));  // open: clr
  Register #(.width(16)) register_3 (.D(dval), .en(demultiplexer_1_out2), .Q(reg2), .clk(clock));  // open: clr
  Register #(.width(16)) register_4 (.D(dval), .en(demultiplexer_1_out3), .Q(reg3), .clk(clock));  // open: clr
  Register #(.width(16)) register_5 (.D(dval), .en(demultiplexer_1_out4), .Q(reg4), .clk(clock));  // open: clr
  Register #(.width(16)) register_6 (.D(dval), .en(demultiplexer_1_out5), .Q(reg5), .clk(clock));  // open: clr
  Register #(.width(16)) register_7 (.D(dval), .en(demultiplexer_1_out6), .Q(reg6), .clk(clock));  // open: clr
  Register #(.width(16)) register_8 (.D(dval), .en(demultiplexer_1_out7), .Q(reg7), .clk(clock));  // open: clr
  Multiplexer #(.select(3), .width(16)) multiplexer_1 (
    .in0(reg0), .in1(reg1), .in2(reg2), .in3(reg3), .in4(reg4), .in5(reg5), .in6(reg6), .in7(reg7),
    .out(sval), .sel(sreg));  // open: en
  Multiplexer #(.select(3), .width(16)) multiplexer_2 (
    .in0(reg0), .in1(reg1), .in2(reg2), .in3(reg3), .in4(reg4), .in5(reg5), .in6(reg6), .in7(reg7),
    .out(tval), .sel(treg));  // open: en
  // Probe on reg0
  // Probe on reg1
  // Probe on reg2
  // Probe on reg3
  // Probe on reg4
  // Probe on reg5
  // Probe on reg6
  // Probe on reg7
endmodule

// ALU
module alu_16bit (
  input  cin,
  input  [15:0] sval,
  input  sinv,
  input  [3:0] aop,
  input  [15:0] tval,
  input  tinv,
  output gt,
  output eq,
  output lt,
  output cout,
  output zero,
  output [15:0] dval
);

  wire or_2_out;
  wire [15:0] adder_1_out, and_1_out, bit_extender_1_out, bit_extender_2_out, bit_extender_3_out,
       invertmux_16bit_1_dval, invertmux_16bit_2_dval, or_1_out, shifter_1_out, shifter_2_out, xor_1_out;

  invertmux_16bit invertmux_16bit_1 (.sval(sval), .invert(sinv), .dval(invertmux_16bit_1_dval));
  invertmux_16bit invertmux_16bit_2 (.sval(tval), .invert(tinv), .dval(invertmux_16bit_2_dval));
  Comparator #(.width(16)) comparator_1 (
    .a(invertmux_16bit_1_dval), .b(invertmux_16bit_2_dval), .gt(gt), .eq(eq), .lt(lt));
  Adder #(.width(16)) adder_1 (
    .a(invertmux_16bit_1_dval), .b(invertmux_16bit_2_dval), .out(adder_1_out), .cin(cin), .cout(cout));
  assign and_1_out = invertmux_16bit_1_dval & invertmux_16bit_2_dval;  // AND_Gate and_1, 16 bits wide
  assign or_1_out = invertmux_16bit_1_dval | invertmux_16bit_2_dval;  // OR_Gate or_1, 16 bits wide
  assign xor_1_out = invertmux_16bit_1_dval ^ invertmux_16bit_2_dval;  // XOR_Gate xor_1, 16 bits wide
  assign bit_extender_1_out = {{15{1'b0}}, lt};  // Bit_Extender bit_extender_1
  Shifter #(.width(16)) shifter_1 (
    .in(invertmux_16bit_1_dval), .\dist (invertmux_16bit_2_dval[3:0]), .out(shifter_1_out));
  Shifter #(.width(16), .shift("lr")) shifter_2 (
    .in(invertmux_16bit_1_dval), .\dist (invertmux_16bit_2_dval[3:0]), .out(shifter_2_out));
  assign bit_extender_2_out = {{15{1'b0}}, eq};  // Bit_Extender bit_extender_2
  assign bit_extender_3_out = {{15{1'b0}}, gt};  // Bit_Extender bit_extender_3
  Multiplexer #(.select(4), .width(16)) multiplexer_1 (
    .in0(xor_1_out), .in1(or_1_out), .in2(and_1_out), .in3(shifter_2_out), .in4(shifter_1_out),
    .in5(adder_1_out), .in6(bit_extender_1_out), .in7(bit_extender_2_out), .in8(bit_extender_3_out),
    .out(dval), .sel(aop));  // open: in9, in10, in11, in12, in13, in14, in15, en
  not not_1 (zero, or_2_out);
  or or_2 (or_2_out, dval[0], dval[1], dval[2], dval[3], dval[4], dval[5], dval[6], dval[7], dval[9], dval[10], dval[11], dval[12], dval[13], dval[14], dval[15], dval[8]);
endmodule

module invertmux_16bit (
  input  [15:0] sval,
  input  invert,
  output [15:0] dval
);

  wire [15:0] not_1_out;

  assign not_1_out = ~sval;  // NOT_Gate not_1, 16 bits wide
  Multiplexer #(.width(16)) multiplexer_1 (.in0(not_1_out), .in1(sval), .out(dval), .sel(invert));  // open: en
endmodule

// PC
module pc_16bit (
  input  [1:0] pcop,
  input  [15:0] addr,
  input  pcset,
  input  clock,
  input  reset,
  output [15:0] pc,
  output [15:0] pc_1
);

  wire [15:0] adder_1_out, adder_2_out, multiplexer_1_out;

  Adder #(.width(16)) adder_1 (.a(pc), .b(16'h1), .out(adder_1_out));  // open: cin, cout
  Adder #(.width(16)) adder_2 (.a(pc), .b(addr), .out(adder_2_out));  // open: cin, cout
  Multiplexer #(.select(2), .width(16)) multiplexer_1 (
    .in0(adder_1_out), .in1(adder_2_out), .in2(addr), .out(multiplexer_1_out), .sel(pcop));  // open: in3, en
  Register #(.width(16)) register_1 (.D(multiplexer_1_out), .en(pcset), .Q(pc), .clk(clock), .clr(reset));
  Adder #(.width(16)) adder_3 (.a(pc), .b(16'h1), .out(pc_1));  // open: cin, cout
endmodule

// ID
module id_16bit (
  input  [15:0] inst,
  input  fetch,
  input  clock,
  output [6:0] op,
  output [2:0] dreg,
  output [2:0] sreg,
  output [2:0] treg
);

  Register #(.width(16)) register_1 (.D(inst), .en(fetch), .Q({treg, sreg, dreg, op}), .clk(clock));  // open: clr
endmodule

// Control
module control (
  input  [6:0] cop,
  input  clock,
  output ssel,
  output tsel,
  output cin,
  output sinv,
  output tinv,
  output [3:0] aop,
  output dset,
  output fset,
  output iset,
  output fetch,
  output pcload,
  output [1:0] pcop,
  output write,
  output [1:0] dsel,
  output timm
);

  wire counter_1_q, not_1_out;
  wire [31:12] rom_1_data;

  // Probe on {1'b0, cop}
  not not_1 (not_1_out, rom_1_data[12]);
  ROM #(.dataWidth(32)) rom_1 (
    .addr({1'b0, cop}),
    .data({rom_1_data[31:20], timm, dsel, write, pcop, pcload, rom_1_data[12], iset, fset, dset, aop, tinv, sinv, cin, tsel, ssel}));  // open: sel
  Counter #(.width(1), .max('h1)) counter_1 (
    .count(not_1_out), .Q(counter_1_q), .clk(clock));  // open: load, D, carry, clr
  // Probe on {rom_1_data[31:20], timm, dsel, write, pcop, pcload, rom_1_data[12], iset, fset, dset, aop, tinv, sinv, cin, tsel, ssel}
  or or_1 (fetch, rom_1_data[12], counter_1_q);

  // Notes on the sheet:
  //   cop: pull=down
  //   contents of rom_1 (hex, n*v repeats v):
  //   3000 2800 30a1
endmodule

module fu (
  input  gt,
  input  eq,
  input  lt,
  input  fset,
  input  cout,
  input  clock,
  input  zero,
  input  br,
  output gt_2,
  output eq_2,
  output lt_2,
  output cout_2,
  output zero_2,
  output br_2
);

  wire [7:6] flags_q;

  Register flags (
    .D({2'b00, br, zero, cout, lt, eq, gt}), .en(fset),
    .Q({flags_q, br_2, zero_2, cout_2, lt_2, eq_2, gt_2}), .clk(clock));  // open: clr
endmodule

module mainv2 (
);

  wire clock, idfetch, immclr, immset, pcset, rclr, reset, rload;
  wire [1:0] pcop;
  wire [2:0] iddreg, idsreg, idtreg;
  wire [6:0] idop;
  wire [15:0] idinst, immdata, immval, pc, pc_1, pcaddr, raddr, rdata;

  Clock clock_1 (.out(clock));
  id_16bit ID (.inst(idinst), .fetch(idfetch), .clock(clock), .op(idop), .dreg(iddreg), .sreg(idsreg), .treg(idtreg));
  pc_16bit u_PC (.addr(pcaddr), .pcop(pcop), .pcset(pcset), .clock(reset), .reset(clock), .pc(pc), .pc_1(pc_1));
  RAM #(.addrWidth(16), .dataWidth(16)) ram_1 (
    .addr(raddr), .data(rdata), .clk(clock), .ld(rload), .clr(rclr));  // open: sel
  Register #(.width(16)) imm (.D(immval), .en(immset), .Q(immdata), .clk(clock), .clr(immclr));
endmodule

module mainv3 (
);

  wire clock_1_out, control_1_cin, control_1_dset, control_1_fetch, control_1_fset, control_1_iset,
       control_1_pcload, control_1_sinv, control_1_ssel, control_1_timm, control_1_tinv, control_1_tsel,
       control_1_write, Line0_dset_2, Line0_iset_2, Line0_ssel_2, Line0_timm_2, Line1_dset_2, Line1_ssel_2,
       Line1_timm_2, Line2_dset_2;
  wire [1:0] control_1_dsel, control_1_pcop, Line0_dsel_2, Line1_dsel_2, Line2_dsel_2;
  wire [2:0] id_16bit_1_dreg, id_16bit_1_sreg, id_16bit_1_treg, Reg0_dreg_2, Reg0_sreg_2, Reg0_treg_2;
  wire [3:0] control_1_aop, Line0_aop_2, Line1_aop_2;
  wire [6:0] id_16bit_1_op;
  wire [15:0] alu_16bit_1_dval, imm_q, multiplexer_1_out, pc_16bit_1_pc, ram_1_data, Reg0_ldata,
       Reg1_immdata, Reg1_ldata, Reg1_sdata, Reg1_tdata, Reg2_immdata, Reg2_ldata, Reg2_tdata,
       registerfile_8x16bit_1_sval, registerfile_8x16bit_1_tval;

  Clock clock_1 (.out(clock_1_out));
  control control_1 (
    .cop(id_16bit_1_op), .clock(clock_1_out), .ssel(control_1_ssel), .tsel(control_1_tsel),
    .cin(control_1_cin), .sinv(control_1_sinv), .tinv(control_1_tinv), .aop(control_1_aop),
    .dset(control_1_dset), .fset(control_1_fset), .iset(control_1_iset), .fetch(control_1_fetch),
    .pcload(control_1_pcload), .pcop(control_1_pcop), .write(control_1_write), .dsel(control_1_dsel),
    .timm(control_1_timm));
  pc_16bit pc_16bit_1 (
    .pcop(control_1_pcop), .pcset(control_1_pcload), .clock(clock_1_out), .pc(pc_16bit_1_pc));  // open: addr, reset, pc_1
  RAM #(.addrWidth(16), .dataWidth(16)) ram_1 (
    .addr(pc_16bit_1_pc), .data(ram_1_data), .clk(clock_1_out));  // open: sel, ld, clr
  id_16bit id_16bit_1 (
    .inst(ram_1_data), .fetch(control_1_fetch), .clock(clock_1_out), .op(id_16bit_1_op),
    .dreg(id_16bit_1_dreg), .sreg(id_16bit_1_sreg), .treg(id_16bit_1_treg));
  regPipe Reg0 (
    .dreg(id_16bit_1_dreg), .sreg(id_16bit_1_sreg), .treg(id_16bit_1_treg), .lval(ram_1_data), .set(1'b1),
    .clock(clock_1_out), .clr(1'b0), .dreg_2(Reg0_dreg_2), .sreg_2(Reg0_sreg_2), .treg_2(Reg0_treg_2),
    .ldata(Reg0_ldata));  // open: immval, sval, tval, immdata, sdata, tdata
  controlPipe Line0 (
    .ssel(control_1_ssel), .tsel(control_1_tsel), .cin(control_1_cin), .sinv(control_1_sinv),
    .tinv(control_1_tinv), .aop(control_1_aop), .dset(control_1_dset), .fset(control_1_fset),
    .iset(control_1_iset), .fetch(control_1_fetch), .pcload(control_1_pcload), .pcop(control_1_pcop),
    .write(control_1_write), .dsel(control_1_dsel), .timm(control_1_timm), .set(1'b1), .clock(clock_1_out),
    .clr(1'b0), .ssel_2(Line0_ssel_2), .aop_2(Line0_aop_2), .dset_2(Line0_dset_2), .iset_2(Line0_iset_2),
    .dsel_2(Line0_dsel_2), .timm_2(Line0_timm_2));  // open: tsel_2, cin_2, sinv_2, tinv_2, fset_2, fetch_2, pcload_2, pcop_2, write_2
  registerFile_8x16bit registerfile_8x16bit_1 (
    .dreg(Reg0_dreg_2), .sreg(Reg0_sreg_2), .treg(Reg0_treg_2), .dval(multiplexer_1_out),
    .dset(Line2_dset_2), .clock(clock_1_out), .sval(registerfile_8x16bit_1_sval),
    .tval(registerfile_8x16bit_1_tval));  // open: reg0, reg1, reg2, reg3, reg4, reg5, reg6, reg7
  Register #(.width(16)) imm (.D(Reg0_ldata), .en(Line0_iset_2), .Q(imm_q), .clk(clock_1_out));  // open: clr
  regPipe Reg1 (
    .immval(imm_q), .sval(registerfile_8x16bit_1_tval), .tval(registerfile_8x16bit_1_sval),
    .lval(Reg0_ldata), .set(1'b1), .clock(clock_1_out), .clr(1'b0), .immdata(Reg1_immdata),
    .sdata(Reg1_sdata), .tdata(Reg1_tdata), .ldata(Reg1_ldata));  // open: dreg, sreg, treg, dreg_2, sreg_2, treg_2
  controlPipe Line1 (
    .ssel(Line0_ssel_2), .aop(Line0_aop_2), .dset(Line0_dset_2), .dsel(Line0_dsel_2), .timm(Line0_timm_2),
    .set(1'b1), .clock(clock_1_out), .clr(1'b0), .ssel_2(Line1_ssel_2), .aop_2(Line1_aop_2),
    .dset_2(Line1_dset_2), .dsel_2(Line1_dsel_2), .timm_2(Line1_timm_2));  // open: tsel, cin, sinv, tinv, fset, iset, fetch, pcload, pcop, write, tsel_2, cin_2, sinv_2, tinv_2, fset_2, iset_2, fetch_2, pcload_2, pcop_2, write_2
  alu_16bit alu_16bit_1 (
    .sval(Reg1_sdata), .tval(Reg1_tdata), .aop(Line1_aop_2), .dval(alu_16bit_1_dval));  // open: cin, sinv, tinv, gt, eq, lt, cout, zero
  regPipe Reg2 (
    .immval(Reg1_immdata), .tval(alu_16bit_1_dval), .lval(Reg1_ldata), .set(1'b1), .clock(clock_1_out),
    .clr(1'b0), .immdata(Reg2_immdata), .tdata(Reg2_tdata), .ldata(Reg2_ldata));  // open: dreg, sreg, treg, sval, dreg_2, sreg_2, treg_2, sdata
  controlPipe Line2 (
    .ssel(Line1_ssel_2), .dset(Line1_dset_2), .dsel(Line1_dsel_2), .timm(Line1_timm_2), .set(1'b1),
    .clock(clock_1_out), .clr(1'b0), .dset_2(Line2_dset_2), .dsel_2(Line2_dsel_2));  // open: tsel, cin, sinv, tinv, aop, fset, iset, fetch, pcload, pcop, write, ssel_2, tsel_2, cin_2, sinv_2, tinv_2, aop_2, fset_2, iset_2, fetch_2, pcload_2, pcop_2, write_2, timm_2
  Multiplexer #(.select(2), .width(16)) multiplexer_1 (
    .in0(Reg2_immdata), .in1(Reg2_ldata), .in2(Reg2_tdata), .out(multiplexer_1_out), .sel(Line2_dsel_2));  // open: in3, en
endmodule

module controlPipe (
  input  ssel,
  input  set,
  input  tsel,
  input  clock,
  input  cin,
  input  sinv,
  input  clr,
  input  tinv,
  input  [3:0] aop,
  input  dset,
  input  fset,
  input  iset,
  input  fetch,
  input  pcload,
  input  [1:0] pcop,
  input  write,
  input  [1:0] dsel,
  input  timm,
  output ssel_2,
  output tsel_2,
  output cin_2,
  output sinv_2,
  output tinv_2,
  output [3:0] aop_2,
  output dset_2,
  output fset_2,
  output iset_2,
  output fetch_2,
  output pcload_2,
  output [1:0] pcop_2,
  output write_2,
  output [1:0] dsel_2,
  output timm_2
);

  wire [31:20] register_1_q;

  Register #(.width(32)) register_1 (
    .D({{12{1'b0}}, timm, dsel, write, pcop, pcload, fetch, iset, fset, dset, aop, tinv, sinv, cin, tsel, ssel}),
    .en(set),
    .Q({register_1_q, timm_2, dsel_2, write_2, pcop_2, pcload_2, fetch_2, iset_2, fset_2, dset_2, aop_2, tinv_2, sinv_2, cin_2, tsel_2, ssel_2}),
    .clk(clock), .clr(clr));
endmodule

module regPipe (
  input  [15:0] immval,
  input  [2:0] dreg,
  input  [2:0] sreg,
  input  [2:0] treg,
  input  [15:0] sval,
  input  [15:0] tval,
  input  [15:0] lval,
  input  set,
  input  clock,
  input  clr,
  output [15:0] immdata,
  output [2:0] dreg_2,
  output [2:0] sreg_2,
  output [2:0] treg_2,
  output [15:0] sdata,
  output [15:0] tdata,
  output [15:0] ldata
);

  Register #(.width(16)) imm (.D(immval), .en(set), .Q(immdata), .clk(clock), .clr(clr));
  Register #(.width(9)) \reg  (.D({dreg, sreg, treg}), .en(set), .Q({dreg_2, sreg_2, treg_2}), .clk(clock), .clr(clr));
  Register #(.width(16)) s (.D(sval), .en(set), .Q(sdata), .clk(clock), .clr(clr));
  Register #(.width(16)) t (.D(tval), .en(set), .Q(tdata), .clk(clock), .clr(clr));
  Register #(.width(16)) l (.D(lval), .en(set), .Q(ldata), .clk(clock), .clr(clr));
endmodule
